# Fritzing sketch fritzing (saved by Fritzing 0.7.12b)
perfboards: 2

parts:
  Nano1 = Arduino Nano v2.3
  S1 = Pushbutton [package="[THT]"]
  S2 = Pushbutton [package="[THT]"]
  S3 = Pushbutton [package="[THT]"]
  S4 = Pushbutton [package="[THT]"]
  U1 = WS2812 RGB LED strip
  U2 = WS2812 RGB LED strip
  U3 = WS2812 RGB LED strip
  U4 = WS2812 RGB LED strip
  Bauteil1 = 12 NeoPixel Ring [part_number=1643]
  Power_plug1 = Power plug  # not connected
  S5 = Toggle Switch [package=THT]
  J1 = Piezo Speaker

nets:
  N1: Nano1.GND, S1.Pin_2, S2.Pin_3, S2.Pin_4, S3.Pin_1, S3.Pin_2, S4.Pin_3, S4.Pin_4, J1.pin1
  N2: Nano1.D2, U2.DIN
  N3: Nano1.D3, S1.Pin_3, S1.Pin_4
  N4: Nano1.D4, U3.DIN
  N5: Nano1.D5, S3.Pin_3
  N6: Nano1.D6, U1.DIN
  N7: Nano1.D7, S2.Pin_1, S2.Pin_2
  N8: Nano1.D8, U4.DIN
  N9: Nano1.D9, S4.Pin_1
  N10: Nano1.D10, Bauteil1.IN
  N11: Nano1.D11, J1.pin2
  N12: Nano1.D13, S5.COM
  N13: Nano1.+5V, S5.L1

custom parts:
  WS2812 RGB LED strip: WS2812 strip
  12 NeoPixel Ring: 12 ultra bright smart LED NeoPixels are arranged in a circle with 1.5" (37mm) outer diameter. The rings are 'chainable' - connect the output pin of one to the input pin of another. Use only one microcontroller pin to control as many as you can chain together! Each LED is addressable as the driver chip is inside the LED. Each one has ~18mA constant current drive so the color will be very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
